// Digital circuit template_01.dig as structural Verilog
module template_01 (
  input  reset,
  input  clk,
  output A,
  output B,
  output C
);

  wire and_1_out, and_2_out, and_3_out, nor_1_out, not_1_out, not_2_out, not_3_out, xnor_1_out, xor_1_out;

  not not_1 (not_1_out, C);
  and and_1 (and_1_out, A, not_1_out);
  xnor xnor_1 (xnor_1_out, B, and_1_out);
  not not_2 (not_2_out, reset);
  xor xor_1 (xor_1_out, A, C);
  nor nor_1 (nor_1_out, A, reset);
  and and_2 (and_2_out, xnor_1_out, not_2_out);
  and and_3 (and_3_out, not_3_out, xor_1_out);
  not not_3 (not_3_out, reset);
  D_FF d_ff_1 (.D(nor_1_out), .C(clk), .Q(A));  // open: nQ
  D_FF d_ff_2 (.D(and_2_out), .C(clk), .Q(B));  // open: nQ
  D_FF d_ff_3 (.D(and_3_out), .C(clk), .Q(C));  // open: nQ

  // Other names for the same wires on the sheet: Rst = reset
endmodule

/* Test case T1:
clk reset C B A
0 0 0 0 0 
0 1 0 0 0
1 1 0 0 0
0 0 0 0 0
1 0 0 1 1
0 0 0 1 1
1 0 1 1 0
0 0 1 1 0 
1 0 1 0 1
0 0 1 0 1
1 0 0 1 0
0 0 0 1 0
1 0 0 0 1
0 0 0 0 1
1 0 1 0 0
0 0 1 0 0
1 0 1 1 1
0 0 1 1 1
1 0 0 0 0
0 0 0 0 0
1 0 0 1 1
0 0 0 1 1
1 0 1 1 0
0 0 1 1 0 
1 0 1 0 1
0 0 1 0 1
1 0 0 1 0
0 0 0 1 0
1 0 0 0 1
0 0 0 0 1
1 0 1 0 0
0 0 1 0 0
1 0 1 1 1
0 0 1 1 1
*/
