// Digital circuit template_02.dig as structural Verilog
module template_02 (
  input  [15:0] A,
  input  \input ,
  input  clk,
  input  [3:0] R,
  output [15:0] nroot,
  output busy
);

  wire acc_gt_a, and_1_out, and_2_out, and_3_out, and_4_out, and_6_out, and_7_out, comparator_1_eq,
       comparator_3_lt, d_ff_1_nq, finish, multiplexer_1_out, next, not_1_out, not_2_out, or_1_out, or_2_out,
       or_3_out, or_4_out, or_5_out, or_7_out, start;
  wire [3:0] add_1_s, cnt, multiplexer_3_out, sub_1_s;
  wire [15:0] mask, multiplexer_4_out, multiplexer_5_out, multiplexer_6_out, multiplexer_7_out,
       multiplexer_8_out, new_base, or_6_out, root;
  wire [31:0] acc, mul_1_mul, multiplexer_2_out;

  and and_1 (and_1_out, busy, next);
  Add #(.Bits(4)) add_1 (.a(cnt), .b(4'b0001), .c_i(1'b0), .s(add_1_s));  // open: c_o
  and and_2 (and_2_out, busy, next);
  Mul #(.Bits(16)) mul_1 (.a(root), .b(acc[15:0]), .mul(mul_1_mul));
  or or_1 (or_1_out, start, and_1_out);
  or or_2 (or_2_out, start, and_2_out);
  D_FF d_ff_1 (.D(\input ), .C(clk), .nQ(d_ff_1_nq));  // open: Q
  Multiplexer multiplexer_1 (.sel(start), .in_0(1'b0), .in_1(1'b1), .out(multiplexer_1_out));
  and and_3 (and_3_out, busy, next);
  Multiplexer #(.Bits(32)) multiplexer_2 (.sel(or_1_out), .in_0(mul_1_mul), .in_1(32'h1), .out(multiplexer_2_out));
  Multiplexer #(.Bits(4)) multiplexer_3 (.sel(or_2_out), .in_0(add_1_s), .in_1(4'b0000), .out(multiplexer_3_out));
  and and_4 (and_4_out, \input , d_ff_1_nq);
  or or_3 (or_3_out, start, finish);
  Multiplexer #(.Bits(16)) multiplexer_4 (
    .sel(start), .in_0({1'b0, mask[15:1]}), .in_1(16'h8000), .out(multiplexer_4_out));
  or or_4 (or_4_out, start, and_3_out);
  Register #(.Bits(4)) register_1 (.D(multiplexer_3_out), .C(clk), .en(1'b1), .Q(cnt));
  not not_1 (not_1_out, busy);
  Register #(.Bits(32)) register_2 (.D(multiplexer_2_out), .C(clk), .en(1'b1), .Q(acc));
  and and_5 (start, not_1_out, and_4_out);
  Register register_3 (.D(multiplexer_1_out), .C(clk), .en(or_3_out), .Q(busy));
  Register #(.Bits(16)) register_4 (.D(multiplexer_4_out), .C(clk), .en(or_4_out), .Q(mask));
  Multiplexer #(.Bits(16)) multiplexer_5 (.sel(acc_gt_a), .in_0(root), .in_1(new_base), .out(multiplexer_5_out));
  and and_6 (and_6_out, busy, next);
  Multiplexer #(.Bits(16)) multiplexer_6 (
    .sel(start), .in_0(multiplexer_5_out), .in_1({16{1'b0}}), .out(multiplexer_6_out));
  or or_5 (or_5_out, start, and_6_out);
  Register #(.Bits(16)) register_5 (.D(multiplexer_6_out), .C(not_2_out), .en(or_5_out), .Q(new_base));
  not not_2 (not_2_out, clk);
  Sub #(.Bits(4)) sub_1 (.a(R), .b(4'b0001), .c_i(1'b0), .s(sub_1_s));  // open: c_o
  Comparator #(.Bits(16)) comparator_1 (.a(mask), .b({16{1'b0}}), .eq(comparator_1_eq));  // open: gt, lt
  Multiplexer #(.Bits(16)) multiplexer_7 (.sel(acc_gt_a), .in_0(root), .in_1(new_base), .out(multiplexer_7_out));
  Comparator #(.Bits(32)) comparator_2 (.a({{16{1'b0}}, A}), .b(acc), .lt(acc_gt_a));  // open: gt, eq
  Comparator #(.Bits(4)) comparator_3 (.a(sub_1_s), .b(cnt), .lt(comparator_3_lt));  // open: gt, eq
  Register #(.Bits(16)) register_6 (.D(new_base), .C(clk), .en(finish), .Q(nroot));
  assign or_6_out = mask | multiplexer_7_out;  // Or or_6, 16 bits wide
  and and_7 (and_7_out, busy, next);
  and and_8 (finish, busy, next, comparator_1_eq);
  or or_7 (or_7_out, start, and_7_out);
  or or_8 (next, acc_gt_a, comparator_3_lt);
  Multiplexer #(.Bits(16)) multiplexer_8 (.sel(start), .in_0(or_6_out), .in_1({16{1'b0}}), .out(multiplexer_8_out));
  Register #(.Bits(16)) register_7 (.D(multiplexer_8_out), .C(clk), .en(or_7_out), .Q(root));

  // Notes on the sheet:
  //   clk: Hz: 200
endmodule

/* Test case TestCase1:
clk A R input nroot busy
0 0 0 0 X 0
1 0 0 0 X 0
0 0 0 0 X 0
1 0 0 0 X 0
0 2 2 1 X X
1 2 2 1 X X
repeat (255) C 2 2 0 X X
0 2 2 0 1 0
1 2 2 0 1 0
0 0 0 0 X 0
1 0 0 0 X 0
0 0 0 0 X 0
1 0 0 0 X 0
0 4 2 1 X X
1 4 2 1 X X
repeat (255) C 4 2 0 X X
0 4 2 0 2 0
1 4 2 0 2 0
0 0 0 0 X 0
1 0 0 0 X 0
0 0 0 0 X 0
1 0 0 0 X 0
0 8 2 1 X X
1 8 2 1 X X
repeat (255) C 8 2 0 X X
0 8 2 0 2 0
1 8 2 0 2 0
0 0 0 0 X 0
1 0 0 0 X 0
0 0 0 0 X 0
1 0 0 0 X 0
0 16 2 1 X X
1 16 2 1 X X
repeat (255) C 16 2 0 X X
0 16 2 0 4 0
1 16 2 0 4 0
*/

/* Test case TestCase4:
clk A R input nroot busy
0 0 0 0 X 0
1 0 0 0 X 0
0 0 0 0 X 0
1 0 0 0 X 0
0 65530 12 1 X X
1 65530 12 1 X X
repeat (255) C 65530 12 0 X X
0 65530 12 0 2 0
1 65530 12 0 2 0
0 0 0 0 X 0
1 0 0 0 X 0
0 0 0 0 X 0
1 0 0 0 X 0
0 60000 3 1 X X
1 60000 3 1 X X
repeat (255) C 60000 3 0 X X
0 60000 3 0 39 0
1 60000 3 0 39 0
0 0 0 0 X 0
1 0 0 0 X 0
0 0 0 0 X 0
1 0 0 0 X 0
0 55124 4 1 X X
1 55124 4 1 X X
repeat (255) C 55124 4 0 X X
0 55124 4 0 15 0
1 55124 4 0 15 0
0 0 0 0 X 0
1 0 0 0 X 0
0 0 0 0 X 0
1 0 0 0 X 0
0 14778 5 1 X X
1 14778 5 1 X X
repeat (255) C 14778 5 0 X X
0 14778 5 0 6 0
1 14778 5 0 6 0
*/

/* Test case TestCase8:
clk A R input nroot busy
0 0 0 0 X 0
1 0 0 0 X 0
0 0 0 0 X 0
1 0 0 0 X 0
0 65535 1 1 X X
1 65535 1 1 X X
repeat (255) C 65535 1 0 X X
0 65535 1 0 65535 0
1 65535 1 0 65535 0
0 0 0 0 X 0
1 0 0 0 X 0
0 0 0 0 X 0
1 0 0 0 X 0
0 64000 15 1 X X
1 64000 15 1 X X
repeat (255) C 64000 15 0 X X
0 64000 15 0 2 0
1 64000 15 0 2 0
0 0 0 0 X 0
1 0 0 0 X 0
0 0 0 0 X 0
1 0 0 0 X 0
0 12000 5 1 X X
1 12000 5 1 X X
repeat (255) C 12000 5 0 X X
0 12000 5 0 6 0
1 12000 5 0 6 0
0 0 0 0 X 0
1 0 0 0 X 0
0 0 0 0 X 0
1 0 0 0 X 0
0 65535 15 1 X X
1 65535 15 1 X X
repeat (255) C 65535 15 0 X X
0 65535 15 0 2 0
1 65535 15 0 2 0
*/
