// Digital circuit 1.dig as structural Verilog
module _1 (
  input  [2:0] A,
  input  [2:0] B
);

  wire not_1_out, not_2_out, not_3_out, not_4_out, S0, S1, S2, S3, Sum_gt_3;

  or or_1 (Sum_gt_3, S2, S3);
  not not_1 (not_1_out, Sum_gt_3);
  Seven_Seg seven_seg_1 (
    .a(not_1_out), .b(1'b1), .c(1'b1), .d(not_4_out), .e(not_2_out), .f(not_3_out), .g(1'b0), .dp(1'b0));
  not not_2 (not_2_out, Sum_gt_3);
  not not_3 (not_3_out, Sum_gt_3);
  Add #(.Bits(3)) add_1 (.a(A), .b(B), .c_i(1'b0), .s({S2, S1, S0}), .c_o(S3));
  not not_4 (not_4_out, Sum_gt_3);
endmodule
