// Digital circuit 2.dig as structural Verilog
module _2 (
  input  [7:0] in,
  output [3:0] out
);

  wire a1, a2;
  wire [2:0] LtoR_num, RtoL_num, sub_1_s;
  wire [3:0] Sum;

  Multiplexer #(.Bits(4)) multiplexer_1 (.sel(a1), .in_0(4'b0000), .in_1(Sum), .out(out));
  PriorityEncoder #(.Selector_Bits(3)) RtoL (
    .in0(in[7]), .in1(in[6]), .in2(in[5]), .in3(in[4]), .in4(in[3]), .in5(in[2]), .in6(in[1]), .in7(in[0]),
    .num(RtoL_num), .any(a1));
  PriorityEncoder #(.Selector_Bits(3)) LtoR (
    .in0(in[0]), .in1(in[1]), .in2(in[2]), .in3(in[3]), .in4(in[4]), .in5(in[5]), .in6(in[6]), .in7(in[7]),
    .num(LtoR_num), .any(a2));
  Sub #(.Bits(3)) sub_1 (.a(3'b111), .b(RtoL_num), .c_i(1'b0), .s(sub_1_s));  // open: c_o
  Add #(.Bits(3)) add_1 (.a(sub_1_s), .b(LtoR_num), .c_i(1'b0), .s(Sum[2:0]), .c_o(Sum[3]));

  // Other names for the same wires on the sheet: S0 = in[0]; S1 = in[1]; S2 = in[2]; S3 = in[3]; S4 = in[4];
  //   S5 = in[5]; S6 = in[6]; S7 = in[7]
endmodule
