// Digital circuit Template-02.dig as structural Verilog
module Template_02 (
  input  [2:0] In,
  input  clk,
  output [7:0] Z
);

  wire and_1_out, and_2_out, and_3_out, and_4_out, and_5_out, and_6_out, and_7_out, and_8_out, not_1_out,
       not_2_out, not_3_out, or_1_out, or_2_out, xor_1_out, xor_2_out, xor_3_out;

  not not_1 (not_1_out, In[2]);
  not not_2 (not_2_out, In[0]);
  not not_3 (not_3_out, In[1]);
  xor xor_1 (xor_1_out, not_1_out, not_3_out);
  and and_1 (and_1_out, In[0], In[1], In[2]);
  or or_1 (or_1_out, In[1], In[2]);
  and and_2 (and_2_out, not_1_out, not_3_out, In[0]);
  xor xor_2 (xor_2_out, In[1], In[2]);
  and and_3 (and_3_out, not_2_out, not_3_out);
  and and_4 (and_4_out, not_1_out, In[0]);
  and and_5 (and_5_out, In[2], not_3_out);
  or or_2 (or_2_out, In[1], In[2]);
  and and_6 (and_6_out, In[1], In[2]);
  and and_7 (and_7_out, xor_1_out, not_2_out);
  and and_8 (and_8_out, not_2_out, or_1_out);
  or or_3 (Z[2], xor_2_out, and_3_out);
  or or_4 (Z[3], and_4_out, and_5_out);
  xor xor_3 (xor_3_out, In[0], or_2_out);
  or or_5 (Z[1], and_7_out, and_1_out);
  or or_6 (Z[0], and_8_out, and_2_out);
  or or_7 (Z[5], xor_3_out, and_6_out);
  Terminal terminal_1 (.D({2'b01, Z[5], 1'b0, Z[3:0]}), .C(clk), .en(1'b1));

  assign {Z[7:6], Z[4]} = 3'b010;
endmodule
