// Digital circuit Template-03.dig as structural Verilog
module Template_03 (
  input  [3:0] In,
  input  [1:0] Selector,
  output [3:0] Output
);

  wire and_1_out, and_2_out, and_3_out, and_4_out, and_5_out, and_6_out, and_7_out, and_8_out, and_9_out,
       and_10_out, and_11_out, and_12_out, and_13_out, and_14_out, and_15_out, and_16_out, and_17_out,
       and_18_out, and_19_out, and_20_out, NA1, NA2, NA3;
  wire [2:0] Cyclic;
  wire [3:0] Excess_3;
  wire [3:1] _642_3, _2421;

  not not_1 (NA1, In[1]);
  not not_2 (Excess_3[0], In[0]);
  and and_1 (and_1_out, NA1, Excess_3[0]);
  and and_2 (and_2_out, In[1], In[0]);
  and and_3 (and_3_out, NA2, In[1]);
  and and_4 (and_4_out, NA2, In[0]);
  and and_5 (and_5_out, In[2], NA1, Excess_3[0]);
  and and_6 (and_6_out, In[2], In[1]);
  and and_7 (and_7_out, In[2], In[0]);
  xor xor_1 (Cyclic[0], In[0], In[1]);
  xor xor_2 (Cyclic[1], In[2], In[1]);
  or or_1 (Cyclic[2], In[2], In[3]);
  and and_8 (and_8_out, In[2], NA1, In[0]);
  and and_9 (and_9_out, In[1], NA2);
  and and_10 (and_10_out, In[2], Excess_3[0]);
  and and_11 (and_11_out, In[2], In[1]);
  and and_12 (and_12_out, In[2], In[0]);
  and and_13 (and_13_out, In[2], In[1]);
  and and_14 (and_14_out, In[1], Excess_3[0]);
  and and_15 (and_15_out, In[2], NA1, In[0]);
  and and_16 (and_16_out, NA2, NA1, In[0]);
  and and_17 (and_17_out, In[2], Excess_3[0]);
  and and_18 (and_18_out, In[2], In[1]);
  and and_19 (and_19_out, In[2], In[0]);
  and and_20 (and_20_out, In[1], In[0]);
  not not_3 (NA3, In[3]);
  not not_4 (NA2, In[2]);
  or or_2 (Excess_3[1], and_1_out, and_2_out);
  or or_3 (Excess_3[2], and_3_out, and_4_out, and_5_out);
  or or_4 (Excess_3[3], and_6_out, In[3], and_7_out);
  or or_5 (_2421[1], and_8_out, In[3], and_9_out);
  or or_6 (_2421[2], and_10_out, In[3], and_11_out);
  or or_7 (_2421[3], and_12_out, In[3], and_13_out);
  or or_8 (_642_3[1], and_14_out, In[3], and_15_out);
  or or_9 (_642_3[2], and_16_out, and_17_out, and_18_out);
  or or_10 (_642_3[3], and_19_out, In[3], and_20_out);
  Multiplexer #(.Selector_Bits(2), .Bits(4)) multiplexer_1 (
    .sel(Selector), .in_0(Excess_3), .in_1({In[3], Cyclic}), .in_2({_2421, In[0]}), .in_3({_642_3, In[0]}),
    .out(Output));

  // Other names for the same wires on the sheet: _642_3[0] = In[0]; _2421[0] = In[0]; A0 = In[0]; Input[3:0] = In;
  //   A1 = In[1]; A2 = In[2]; A3 = In[3]; Cyclic[3] = In[3]; NA0 = Excess_3[0]
endmodule
