// Digital circuit Template-04.dig as structural Verilog
module Template_04 (
  input  [6:0] In,
  output [6:0] Output
);

  wire E1, E2, E3, E4, E5, E6, E7, S1, S2, S3;

  xor xor_1 (S1, In[6], In[4], In[2], In[0]);
  xor xor_2 (S2, In[5], In[4], In[1], In[0]);
  xor xor_3 (S3, In[3], In[2], In[1], In[0]);
  Decoder #(.Selector_Bits(3)) decoder_1 (
    .sel({S3, S2, S1}), .out_1(E1), .out_2(E2), .out_3(E3), .out_4(E4), .out_5(E5), .out_6(E6), .out_7(E7));  // open: out_0
  xor xor_4 (Output[6], In[6], E1);
  xor xor_5 (Output[5], In[5], E2);
  xor xor_6 (Output[4], In[4], E3);
  xor xor_7 (Output[3], In[3], E4);
  xor xor_8 (Output[2], In[2], E5);
  xor xor_9 (Output[1], In[1], E6);
  xor xor_10 (Output[0], In[0], E7);

  // Other names for the same wires on the sheet: M4 = In[0]; M3 = In[1]; M2 = In[2]; P3 = In[3]; M1 = In[4];
  //   P2 = In[5]; P1 = In[6]; O1 = Output[6]; O2 = Output[5]; O3 = Output[4]; O4 = Output[3]; O5 = Output[2];
  //   O6 = Output[1]; O7 = Output[0]
endmodule
