// Digital circuit Template.dig as structural Verilog
module Template (
  input  A,
  input  B,
  input  C,
  input  D,
  output Before,
  output After
);

  wire and_1_out, and_2_out, and_3_out, and_4_out, and_5_out, not_1_out;

  not not_1 (not_1_out, B);
  and and_1 (and_1_out, ~C, D);  // And
  and and_2 (and_2_out, A, ~B, D);  // And
  and and_3 (and_3_out, ~C, D);  // And
  and and_4 (and_4_out, A, ~B, D);  // And
  and and_5 (and_5_out, not_1_out, D);
  or or_1 (Before, and_1_out, ~A, and_2_out);  // Or
  or or_2 (After, and_3_out, ~A, and_4_out, and_5_out);  // Or
endmodule

/* Test case T1:
A B C D Before After
0 0 1 1 1 1
1 0 1 1 1 1
1 0 1 1 1 1
0 0 1 1 1 1
0 0 1 1 1 1
1 0 1 1 1 1
1 0 1 1 1 1
*/
