// Digital circuit Template.dig as structural Verilog
module Template (
  input  P,
  input  T,
  input  D,
  input  C,
  input  B,
  input  A,
  input  Clr,
  input  Load,
  input  Clock,
  output QD,
  output QC,
  output QB,
  output QA,
  output RCO
);

  wire and_1_out, and_2_out, and_3_out, and_4_out, and_5_out, and_6_out, and_7_out, and_8_out, and_9_out,
       and_10_out, and_11_out, and_12_out, Clr_Eff, DA, DB, DC, DD, NA, NB, NC, ND, not_1_out, not_2_out,
       not_3_out, not_4_out, not_11_out, NP, NT, or_1_out, or_2_out, or_3_out, or_4_out, xor_1_out,
       xor_2_out, xor_3_out, xor_4_out;

  not not_1 (not_1_out, Load);
  not not_2 (not_2_out, Load);
  not not_3 (not_3_out, Load);
  not not_4 (not_4_out, Load);
  and and_1 (and_1_out, P, T);
  and and_2 (and_2_out, not_1_out, A);
  and and_3 (and_3_out, P, T, QA);
  and and_4 (and_4_out, not_2_out, B);
  and and_5 (and_5_out, P, T, QA, QB);
  and and_6 (and_6_out, not_3_out, C);
  and and_7 (and_7_out, P, T, QA, QB, QC);
  and and_8 (and_8_out, not_4_out, D);
  xor xor_1 (xor_1_out, and_1_out, QA);
  xor xor_2 (xor_2_out, and_3_out, QB);
  xor xor_3 (xor_3_out, and_5_out, QC);
  xor xor_4 (xor_4_out, and_7_out, QD);
  and and_9 (and_9_out, xor_1_out, Load);
  and and_10 (and_10_out, xor_2_out, Load);
  and and_11 (and_11_out, xor_3_out, Load);
  and and_12 (and_12_out, xor_4_out, Load);
  not not_5 (NA, A);
  not not_6 (NB, B);
  not not_7 (NC, C);
  not not_8 (ND, D);
  not not_9 (NP, P);
  not not_10 (NT, T);
  not not_11 (not_11_out, Load);
  or or_1 (or_1_out, and_9_out, and_2_out);
  or or_2 (or_2_out, and_10_out, and_4_out);
  or or_3 (or_3_out, and_11_out, and_6_out);
  or or_4 (or_4_out, and_12_out, and_8_out);
  or or_5 (Clr_Eff, Clr, not_11_out);
  and and_13 (RCO, QA, QB, QC, QD);
  and and_14 (DA, Clr_Eff, or_1_out);
  and and_15 (DB, Clr_Eff, or_2_out);
  and and_16 (DC, Clr_Eff, or_3_out);
  and and_17 (DD, Clr_Eff, or_4_out);
  D_FF d_ff_1 (.D(DA), .C(Clock), .Q(QA));  // open: nQ
  D_FF d_ff_2 (.D(DB), .C(Clock), .Q(QB));  // open: nQ
  D_FF d_ff_3 (.D(DC), .C(Clock), .Q(QC));  // open: nQ
  D_FF d_ff_4 (.D(DD), .C(Clock), .Q(QD));  // open: nQ

  // Other names for the same wires on the sheet: Clk = Clock
endmodule
