// Digital circuit Template.dig as structural Verilog
module Template (
  input  A,
  input  B,
  input  Clr,
  input  Clock,
  output Z
);

  wire and_1_out, and_2_out, and_3_out, NS, or_1_out, S, xor_1_out;

  xor xor_1 (xor_1_out, A, B, S);
  and and_1 (and_1_out, A, B);
  and and_2 (and_2_out, A, S);
  and and_3 (and_3_out, B, S);
  and and_4 (Z, xor_1_out, Clr);
  D_FF d_ff_1 (.D(NS), .C(Clock), .Q(S));  // open: nQ
  or or_1 (or_1_out, and_1_out, and_2_out, and_3_out);
  and and_5 (NS, or_1_out, Clr);

  // Other names for the same wires on the sheet: Clk = Clock
endmodule
