// Digital circuit Template.dig as structural Verilog
module Template (
  input  P,
  input  Clr,
  input  clock,
  output Z
);

  wire and_1_out, and_2_out, not_1_out, not_2_out, not_3_out, Q, QP;

  and and_1 (and_1_out, P, not_1_out);
  not not_1 (not_1_out, Clr);
  D_FF d_ff_1 (.D(and_1_out), .C(clock), .Q(QP));  // open: nQ
  not not_2 (not_2_out, Clr);
  not not_3 (not_3_out, Q);
  D_FF d_ff_2 (.D(QP), .C(clock), .Q(Q));  // open: nQ
  and and_2 (and_2_out, QP, not_2_out, not_3_out);
  D_FF d_ff_3 (.D(and_2_out), .C(clock), .Q(Z));  // open: nQ

  // Other names for the same wires on the sheet: Clk = clock
endmodule
