// Digital circuit Template.dig as structural Verilog
module Template (
  input  P,
  input  Clr,
  input  clock,
  output Z
);

  wire A, and_1_out, and_2_out, not_1_out, not_2_out, not_3_out, or_1_out;

  or or_1 (or_1_out, A, Z);
  not not_1 (not_1_out, Clr);
  and and_1 (and_1_out, P, not_1_out, or_1_out);
  not not_2 (not_2_out, Clr);
  not not_3 (not_3_out, or_1_out);
  and and_2 (and_2_out, P, not_2_out, not_3_out);
  D_FF d_ff_1 (.D(and_1_out), .C(clock), .Q(A));  // open: nQ
  D_FF d_ff_2 (.D(and_2_out), .C(clock), .Q(Z));  // open: nQ

  // Other names for the same wires on the sheet: B = Z; Clk = clock
endmodule
