// Digital circuit Template.dig as structural Verilog
module Template (
  input  P5,
  input  reset,
  input  clock,
  input  P10,
  input  P20,
  input  Pcoffee,
  input  Ptea,
  input  Pchange,
  input  Pnext,
  output [5:0] Balance,
  output CoffeeOut,
  output TeaOut,
  output [1:0] Change5,
  output [1:0] Change10,
  output [1:0] Change20
);

  wire add5, add10, add20, buyC, buyT, C5, C10, C20, comparator_1_eq, comparator_2_lt, comparator_3_eq,
       comparator_4_lt, comparator_5_eq, comparator_6_lt, comparator_7_eq, comparator_8_lt, comparator_9_eq,
       comparator_10_lt, comparator_11_eq, comparator_12_lt, comparator_13_eq, comparator_14_lt,
       comparator_15_eq, comparator_16_lt, d_ff_1_q, d_ff_2_q, d_ff_3_q, d_ff_4_q, d_ff_5_q, d_ff_6_q,
       d_ff_7_q, d_ff_8_nq, d_ff_9_nq, d_ff_10_nq, d_ff_11_nq, d_ff_12_nq, d_ff_13_nq, d_ff_14_nq,
       decoder_1_out_0, decoder_2_out_0, decoder_3_out_1, decoder_4_out_1, decoder_5_out_0, decoder_6_out_0,
       decoder_7_out_0, decoder_8_out_1, or_2_out, or_3_out, or_4_out, P5_pulse, P10_pulse, P20_pulse,
       Pchange_pulse, Pcoff_pulse, Pnext_pulse, Ptea_pulse;
  wire [1:0] add_2_s, add_3_s, add_4_s, multiplexer_16_out, multiplexer_21_out, multiplexer_23_out;
  wire [2:0] multiplexer_10_out, multiplexer_12_out, multiplexer_15_out, multiplexer_18_out,
       multiplexer_22_out, nextState, S0, S1, S2, S3, S4, state;
  wire [5:0] add_1_s, multiplexer_1_out, multiplexer_2_out, multiplexer_3_out, multiplexer_4_out,
       multiplexer_5_out, multiplexer_6_out, multiplexer_7_out, multiplexer_8_out, multiplexer_9_out,
       or_1_out;

  Multiplexer #(.Bits(6)) multiplexer_1 (.sel(add5), .in_0({6{1'b0}}), .in_1(6'b000101), .out(multiplexer_1_out));
  Multiplexer #(.Bits(6)) multiplexer_2 (.sel(add20), .in_0({6{1'b0}}), .in_1(6'b010100), .out(multiplexer_2_out));
  Multiplexer #(.Bits(6)) multiplexer_3 (.sel(buyT), .in_0({6{1'b0}}), .in_1(6'b101100), .out(multiplexer_3_out));
  Multiplexer #(.Bits(6)) multiplexer_4 (.sel(C10), .in_0({6{1'b0}}), .in_1(6'b110110), .out(multiplexer_4_out));
  Multiplexer #(.Bits(6)) multiplexer_5 (.sel(add10), .in_0({6{1'b0}}), .in_1(6'b001010), .out(multiplexer_5_out));
  Multiplexer #(.Bits(6)) multiplexer_6 (.sel(buyC), .in_0({6{1'b0}}), .in_1(6'b100111), .out(multiplexer_6_out));
  Multiplexer #(.Bits(6)) multiplexer_7 (.sel(C20), .in_0({6{1'b0}}), .in_1(6'b101100), .out(multiplexer_7_out));
  Multiplexer #(.Bits(6)) multiplexer_8 (.sel(C5), .in_0({6{1'b0}}), .in_1(6'b111011), .out(multiplexer_8_out));
  Comparator #(.Bits(3)) comparator_1 (.a(state), .b(3'b011), .eq(comparator_1_eq));  // open: gt, lt
  Comparator #(.Bits(6)) comparator_2 (.a(Balance), .b(6'b010100), .lt(comparator_2_lt));  // open: gt, eq
  Comparator #(.Bits(3)) comparator_3 (.a(state), .b(3'b101), .eq(comparator_3_eq));  // open: gt, lt
  Comparator #(.Bits(6)) comparator_4 (.a(Balance), .b(6'b000101), .lt(comparator_4_lt));  // open: gt, eq
  Comparator #(.Bits(3)) comparator_5 (.a(state), .b(3'b000), .eq(comparator_5_eq));  // open: gt, lt
  Comparator #(.Bits(6)) comparator_6 (.a(Balance), .b(6'b101110), .lt(comparator_6_lt));  // open: gt, eq
  Comparator #(.Bits(3)) comparator_7 (.a(state), .b(3'b000), .eq(comparator_7_eq));  // open: gt, lt
  Comparator #(.Bits(6)) comparator_8 (.a(Balance), .b(6'b101001), .lt(comparator_8_lt));  // open: gt, eq
  Decoder decoder_1 (.sel(comparator_2_lt), .out_0(decoder_1_out_0));  // open: out_1
  Decoder decoder_2 (.sel(comparator_4_lt), .out_0(decoder_2_out_0));  // open: out_1
  Decoder decoder_3 (.sel(comparator_6_lt), .out_1(decoder_3_out_1));  // open: out_0
  Decoder decoder_4 (.sel(comparator_8_lt), .out_1(decoder_4_out_1));  // open: out_0
  assign or_1_out = multiplexer_1_out | multiplexer_5_out | multiplexer_2_out | multiplexer_6_out | multiplexer_3_out | multiplexer_7_out | multiplexer_4_out | multiplexer_8_out;  // Or or_1, 6 bits wide
  and and_1 (C20, comparator_1_eq, decoder_1_out_0);
  and and_2 (C5, comparator_3_eq, decoder_2_out_0);
  and and_3 (add5, comparator_5_eq, P5_pulse, decoder_3_out_1);
  and and_4 (add10, comparator_7_eq, P10_pulse, decoder_4_out_1);
  Add #(.Bits(6)) add_1 (.a(Balance), .b(or_1_out), .c_i(1'b0), .s(add_1_s));  // open: c_o
  D_FF d_ff_1 (.D(P5), .C(clock), .Q(d_ff_1_q));  // open: nQ
  D_FF d_ff_2 (.D(P10), .C(clock), .Q(d_ff_2_q));  // open: nQ
  D_FF d_ff_3 (.D(P20), .C(clock), .Q(d_ff_3_q));  // open: nQ
  D_FF d_ff_4 (.D(Pcoffee), .C(clock), .Q(d_ff_4_q));  // open: nQ
  D_FF d_ff_5 (.D(Ptea), .C(clock), .Q(d_ff_5_q));  // open: nQ
  D_FF d_ff_6 (.D(Pchange), .C(clock), .Q(d_ff_6_q));  // open: nQ
  D_FF d_ff_7 (.D(Pnext), .C(clock), .Q(d_ff_7_q));  // open: nQ
  Multiplexer #(.Bits(6)) multiplexer_9 (.sel(reset), .in_0(add_1_s), .in_1({6{1'b0}}), .out(multiplexer_9_out));
  Comparator #(.Bits(3)) comparator_9 (.a(state), .b(3'b100), .eq(comparator_9_eq));  // open: gt, lt
  Comparator #(.Bits(6)) comparator_10 (.a(Balance), .b(6'b001010), .lt(comparator_10_lt));  // open: gt, eq
  Comparator #(.Bits(3)) comparator_11 (.a(state), .b(3'b000), .eq(comparator_11_eq));  // open: gt, lt
  Comparator #(.Bits(6)) comparator_12 (.a(Balance), .b(6'b011001), .lt(comparator_12_lt));  // open: gt, eq
  Comparator #(.Bits(3)) comparator_13 (.a(state), .b(3'b000), .eq(comparator_13_eq));  // open: gt, lt
  Comparator #(.Bits(6)) comparator_14 (.a(Balance), .b(6'b010100), .lt(comparator_14_lt));  // open: gt, eq
  Comparator #(.Bits(3)) comparator_15 (.a(state), .b(3'b000), .eq(comparator_15_eq));  // open: gt, lt
  Comparator #(.Bits(6)) comparator_16 (.a(Balance), .b(6'b011111), .lt(comparator_16_lt));  // open: gt, eq
  D_FF d_ff_8 (.D(d_ff_1_q), .C(clock), .nQ(d_ff_8_nq));  // open: Q
  D_FF d_ff_9 (.D(d_ff_2_q), .C(clock), .nQ(d_ff_9_nq));  // open: Q
  D_FF d_ff_10 (.D(d_ff_3_q), .C(clock), .nQ(d_ff_10_nq));  // open: Q
  D_FF d_ff_11 (.D(d_ff_4_q), .C(clock), .nQ(d_ff_11_nq));  // open: Q
  D_FF d_ff_12 (.D(d_ff_5_q), .C(clock), .nQ(d_ff_12_nq));  // open: Q
  D_FF d_ff_13 (.D(d_ff_6_q), .C(clock), .nQ(d_ff_13_nq));  // open: Q
  D_FF d_ff_14 (.D(d_ff_7_q), .C(clock), .nQ(d_ff_14_nq));  // open: Q
  Decoder decoder_5 (.sel(comparator_10_lt), .out_0(decoder_5_out_0));  // open: out_1
  Decoder decoder_6 (.sel(comparator_12_lt), .out_0(decoder_6_out_0));  // open: out_1
  Decoder decoder_7 (.sel(comparator_14_lt), .out_0(decoder_7_out_0));  // open: out_1
  Decoder decoder_8 (.sel(comparator_16_lt), .out_1(decoder_8_out_1));  // open: out_0
  and and_5 (P5_pulse, d_ff_1_q, d_ff_8_nq);
  and and_6 (P10_pulse, d_ff_2_q, d_ff_9_nq);
  and and_7 (P20_pulse, d_ff_3_q, d_ff_10_nq);
  and and_8 (Pcoff_pulse, d_ff_4_q, d_ff_11_nq);
  and and_9 (Ptea_pulse, d_ff_5_q, d_ff_12_nq);
  and and_10 (Pchange_pulse, d_ff_6_q, d_ff_13_nq);
  and and_11 (Pnext_pulse, d_ff_7_q, d_ff_14_nq);
  Register #(.Bits(6)) register_1 (.D(multiplexer_9_out), .C(clock), .en(1'b1), .Q(Balance));
  and and_12 (C10, comparator_9_eq, decoder_5_out_0);
  and and_13 (buyC, comparator_11_eq, Pcoff_pulse, decoder_6_out_0);
  and and_14 (buyT, comparator_13_eq, Ptea_pulse, decoder_7_out_0);
  and and_15 (add20, comparator_15_eq, P20_pulse, decoder_8_out_1);
  Multiplexer #(.Bits(3)) multiplexer_10 (.sel(Pnext_pulse), .in_0(3'b001), .in_1(3'b000), .out(multiplexer_10_out));
  Multiplexer #(.Bits(3)) multiplexer_11 (.sel(C20), .in_0(3'b100), .in_1(3'b011), .out(S3));
  Multiplexer #(.Bits(3)) multiplexer_12 (.sel(buyT), .in_0(3'b000), .in_1(3'b010), .out(multiplexer_12_out));
  Multiplexer #(.Bits(3)) multiplexer_13 (.sel(Pchange_pulse), .in_0(multiplexer_10_out), .in_1(3'b011), .out(S1));
  Multiplexer #(.Bits(3)) multiplexer_14 (.sel(C10), .in_0(3'b101), .in_1(3'b100), .out(S4));
  Add #(.Bits(2)) add_2 (.a({1'b0, C10}), .b(Change10), .c_i(1'b0), .s(add_2_s));  // open: c_o
  or or_2 (or_2_out, reset, Pchange_pulse);
  Multiplexer #(.Bits(3)) multiplexer_15 (
    .sel(buyC), .in_0(multiplexer_12_out), .in_1(3'b001), .out(multiplexer_15_out));
  Multiplexer #(.Bits(2)) multiplexer_16 (.sel(or_2_out), .in_0(add_2_s), .in_1(2'b00), .out(multiplexer_16_out));
  Multiplexer #(.Bits(3)) multiplexer_17 (.sel(Pchange_pulse), .in_0(multiplexer_15_out), .in_1(3'b011), .out(S0));
  Multiplexer #(.Bits(3)) multiplexer_18 (.sel(Pnext_pulse), .in_0(3'b010), .in_1(3'b000), .out(multiplexer_18_out));
  Register #(.Bits(2)) register_2 (.D(multiplexer_16_out), .C(clock), .en(1'b1), .Q(Change10));
  Multiplexer #(.Bits(3)) multiplexer_19 (.sel(Pchange_pulse), .in_0(multiplexer_18_out), .in_1(3'b011), .out(S2));
  Add #(.Bits(2)) add_3 (.a({1'b0, C5}), .b(Change5), .c_i(1'b0), .s(add_3_s));  // open: c_o
  or or_3 (or_3_out, reset, Pchange_pulse);
  Decoder #(.Selector_Bits(3)) decoder_9 (
    .sel(state), .out_1(CoffeeOut), .out_2(TeaOut));  // open: out_0, out_3, out_4, out_5, out_6, out_7
  Multiplexer #(.Bits(3), .Selector_Bits(3)) multiplexer_20 (
    .sel(state), .in_0(S0), .in_1(S1), .in_2(S2), .in_3(S3), .in_4(S4), .in_5(3'b000), .in_6(3'b000),
    .in_7(3'b000), .out(nextState));
  Multiplexer #(.Bits(2)) multiplexer_21 (.sel(or_3_out), .in_0(add_3_s), .in_1(2'b00), .out(multiplexer_21_out));
  Add #(.Bits(2)) add_4 (.a({1'b0, C20}), .b(Change20), .c_i(1'b0), .s(add_4_s));  // open: c_o
  or or_4 (or_4_out, reset, Pchange_pulse);
  Multiplexer #(.Bits(3)) multiplexer_22 (.sel(reset), .in_0(nextState), .in_1(3'b000), .out(multiplexer_22_out));
  Multiplexer #(.Bits(2)) multiplexer_23 (.sel(or_4_out), .in_0(add_4_s), .in_1(2'b00), .out(multiplexer_23_out));
  Register #(.Bits(2)) register_3 (.D(multiplexer_21_out), .C(clock), .en(1'b1), .Q(Change5));
  Register #(.Bits(3)) register_4 (.D(multiplexer_22_out), .C(clock), .en(1'b1), .Q(state));
  Register #(.Bits(2)) register_5 (.D(multiplexer_23_out), .C(clock), .en(1'b1), .Q(Change20));

  // Other names for the same wires on the sheet: Bal[5:0] = Balance; Clk = clock; coffOut = CoffeeOut;
  //   Pcoff = Pcoffee; Pnxt = Pnext; Rst = reset
endmodule
