// Digital circuit Template.dig as structural Verilog
module Template (
  input  [3:0] A,
  input  [3:0] B,
  input  [2:0] S,
  input  M,
  input  C,
  output [3:0] F,
  output Cout
);

  wire Cout0, Cout1, Cout2, Cout3, Cout4, Cout5;
  wire [3:0] add_1_s, add_2_s, add_3_s, add_4_s, add_5_s, add_6_s, and_1_out, and_2_out, M0, M1, NA,
       nand_1_out, NB, nor_1_out, or_1_out, xnor_1_out;

  assign nand_1_out = ~(A & B);  // NAnd nand_1, 4 bits wide
  assign nor_1_out = ~(A | B);  // NOr nor_1, 4 bits wide
  assign xnor_1_out = ~(A ^ B);  // XNOr xnor_1, 4 bits wide
  assign and_1_out = A & B;  // And and_1, 4 bits wide
  assign or_1_out = A | B;  // Or or_1, 4 bits wide
  assign and_2_out = A & NB;  // And and_2, 4 bits wide
  Add #(.Bits(4)) add_1 (.a(A), .b(4'b0000), .c_i(C), .s(add_1_s), .c_o(Cout0));
  Add #(.Bits(4)) add_2 (.a(A), .b(4'b1111), .c_i(C), .s(add_2_s), .c_o(Cout1));
  Add #(.Bits(4)) add_3 (.a(A), .b(B), .c_i(C), .s(add_3_s), .c_o(Cout2));
  Add #(.Bits(4)) add_4 (.a(A), .b(NB), .c_i(C), .s(add_4_s), .c_o(Cout3));
  Add #(.Bits(4)) add_5 (.a(NA), .b(4'b0000), .c_i(C), .s(add_5_s), .c_o(Cout4));
  Add #(.Bits(4)) add_6 (.a(4'b0000), .b(B), .c_i(C), .s(add_6_s), .c_o(Cout5));
  assign NA = ~A;  // Not not_1, 4 bits wide
  assign NB = ~B;  // Not not_2, 4 bits wide
  Multiplexer #(.Selector_Bits(3), .Bits(4)) multiplexer_1 (
    .sel(S), .in_0(NA), .in_1(nand_1_out), .in_2(nor_1_out), .in_3(xnor_1_out), .in_4(and_1_out),
    .in_5(or_1_out), .in_6(and_2_out), .in_7(A), .out(M0));
  Multiplexer #(.Bits(4)) multiplexer_2 (.sel(M), .in_0(M0), .in_1(M1), .out(F));
  Multiplexer #(.Selector_Bits(3)) multiplexer_3 (
    .sel(S), .in_0(Cout0), .in_1(Cout1), .in_2(Cout2), .in_3(Cout3), .in_4(Cout4), .in_5(Cout5), .in_6(1'b0),
    .in_7(1'b0), .out(Cout));
  Multiplexer #(.Selector_Bits(3), .Bits(4)) multiplexer_4 (
    .sel(S), .in_0(add_1_s), .in_1(add_2_s), .in_2(add_3_s), .in_3(add_4_s), .in_4(add_5_s), .in_5(add_6_s),
    .in_6({A[2:0], 1'b0}), .in_7({1'b0, A[3:1]}), .out(M1));
endmodule
