// Digital circuit MasterSlave_JK_FlipFlop.dig as structural Verilog
module MasterSlave_JK_FlipFlop (
  input  J,
  input  K,
  input  Clear,
  input  Clock,
  output Q,
  output Q_2
);

  wire and_1_out, and_2_out, and_3_out, and_4_out, nClear, nClk, nP, P;

  and and_1 (and_1_out, K, Clock, Q);
  and and_2 (and_2_out, J, Clock, Q_2, nClear);
  not not_1 (nClk, Clock);
  not not_2 (nClear, Clear);
  nor nor_1 (P, and_1_out, Clear, nP);
  nor nor_2 (nP, and_2_out, P);
  and and_3 (and_3_out, nP, nClk);
  and and_4 (and_4_out, P, nClk, nClear);
  nor nor_3 (Q, and_3_out, Clear, Q_2);
  nor nor_4 (Q_2, and_4_out, Q);

  // Other names for the same wires on the sheet: Clk = Clock; nQ = Q_2

  // Notes on the sheet:
  //   Master Stage
  //   Slave Stage
endmodule

/* Test case:
K J \Clear Clock Q \Q
0 0 1 0 0 1
0 0 1 1 0 1
0 1 0 0 0 1
0 1 0 1 0 1
0 1 0 0 1 0
1 0 0 1 1 0
1 0 0 0 0 1
0 0 0 1 0 1
0 0 0 0 0 1
0 1 0 1 0 1
0 1 0 0 1 0
*/
