// Digital circuit Template.dig as structural Verilog
module Template (
  input  T,
  input  Clear,
  input  Clock,
  output Q,
  output Q_2
);

  wire Clear_t, inD, nClk, ND, nor_1_out, nor_2_out, nor_3_out, nor_4_out, xor_1_out;

  not not_1 (ND, T);
  not not_2 (Clear_t, Clear);
  not not_3 (nClk, Clock);
  nor nor_1 (nor_1_out, nor_4_out, nor_2_out);
  nor nor_2 (nor_2_out, nor_1_out, nClk);
  nor nor_3 (nor_3_out, nor_2_out, nClk, nor_4_out);
  nor nor_4 (nor_4_out, nor_3_out, inD);
  xor xor_1 (xor_1_out, Q, T);
  and and_1 (inD, xor_1_out, Clear_t);
  nor nor_5 (Q, nor_2_out, Q_2);
  nor nor_6 (Q_2, Q, nor_3_out);

  // Other names for the same wires on the sheet: Clk = Clock; D = T
endmodule
