// Digital circuit Template.dig as structural Verilog
module Template (
  input  A,
  input  B,
  input  Cin,
  output Sum,
  output Cout
);

  wire and_1_out, and_2_out, and_3_out, and_4_out, and_5_out, and_6_out, and_7_out, and_8_out, and_9_out,
       and_10_out, and_11_out, and_12_out, and_13_out, and_14_out, and_15_out, and_16_out, not_1_out,
       not_2_out, not_3_out, or_1_out, or_2_out, or_3_out, or_4_out;

  not not_1 (not_1_out, B);
  not not_2 (not_2_out, Cin);
  not not_3 (not_3_out, A);
  and and_1 (and_1_out, not_3_out, B);
  and and_2 (and_2_out, A, not_1_out);
  and and_3 (and_3_out, A, B);
  and and_4 (and_4_out, not_3_out, B);
  and and_5 (and_5_out, A, not_1_out);
  and and_6 (and_6_out, A, B);
  and and_7 (and_7_out, A, B);
  and and_8 (and_8_out, not_3_out, not_1_out);
  and and_9 (and_9_out, and_1_out, not_2_out);
  and and_10 (and_10_out, and_2_out, not_2_out);
  and and_11 (and_11_out, and_3_out, Cin);
  and and_12 (and_12_out, and_4_out, Cin);
  and and_13 (and_13_out, and_5_out, Cin);
  and and_14 (and_14_out, and_6_out, not_2_out);
  and and_15 (and_15_out, and_7_out, Cin);
  and and_16 (and_16_out, and_8_out, Cin);
  or or_1 (or_1_out, and_16_out, and_9_out);
  or or_2 (or_2_out, and_10_out, and_11_out);
  or or_3 (or_3_out, and_12_out, and_13_out);
  or or_4 (or_4_out, and_14_out, and_15_out);
  or or_5 (Sum, or_1_out, or_2_out);
  or or_6 (Cout, or_3_out, or_4_out);
endmodule
