// Digital circuit Template.dig as structural Verilog
module Template (
  input  A,
  input  B,
  input  Cin,
  output Sum,
  output Cout
);

  wire and_1_out, and_2_out, and_3_out, and_4_out, not_1_out, not_2_out, not_3_out, or_1_out, or_2_out,
       or_3_out, or_4_out, or_5_out, or_6_out, or_7_out, or_8_out, or_9_out, or_10_out, or_11_out, or_12_out,
       or_13_out, or_14_out, or_15_out, or_16_out;

  not not_1 (not_1_out, B);
  not not_2 (not_2_out, Cin);
  not not_3 (not_3_out, A);
  or or_1 (or_1_out, A, B);
  or or_2 (or_2_out, A, not_1_out);
  or or_3 (or_3_out, not_3_out, B);
  or or_4 (or_4_out, not_3_out, not_1_out);
  or or_5 (or_5_out, A, B);
  or or_6 (or_6_out, A, B);
  or or_7 (or_7_out, A, not_1_out);
  or or_8 (or_8_out, not_3_out, B);
  or or_9 (or_9_out, or_1_out, Cin);
  or or_10 (or_10_out, or_2_out, not_2_out);
  or or_11 (or_11_out, or_3_out, not_2_out);
  or or_12 (or_12_out, or_4_out, Cin);
  or or_13 (or_13_out, or_5_out, Cin);
  or or_14 (or_14_out, or_6_out, not_2_out);
  or or_15 (or_15_out, or_7_out, Cin);
  or or_16 (or_16_out, or_8_out, Cin);
  and and_1 (and_1_out, or_9_out, or_10_out);
  and and_2 (and_2_out, or_11_out, or_12_out);
  and and_3 (and_3_out, or_13_out, or_14_out);
  and and_4 (and_4_out, or_15_out, or_16_out);
  and and_5 (Sum, and_1_out, and_2_out);
  and and_6 (Cout, and_3_out, and_4_out);
endmodule
