// Digital circuit Template.dig as structural Verilog
module Template (
  input  A,
  input  B,
  input  C,
  input  D,
  output Z1,
  output Z2,
  output Z3
);

  wire not_1_out, not_2_out, not_3_out, not_4_out, or_1_out, or_2_out, or_3_out, or_4_out, or_5_out,
       or_6_out, or_7_out, or_8_out, or_9_out, or_10_out, or_11_out, or_12_out, or_13_out, or_14_out,
       or_15_out, or_16_out, or_17_out, or_18_out, or_19_out, or_20_out, or_21_out, or_22_out, or_23_out,
       or_24_out, or_25_out, or_26_out, or_27_out, or_28_out, or_29_out, or_30_out, or_31_out, or_32_out;

  not not_1 (not_1_out, C);
  not not_2 (not_2_out, D);
  not not_3 (not_3_out, A);
  not not_4 (not_4_out, B);
  or or_1 (or_1_out, A, B, C, D);
  or or_2 (or_2_out, A, B, C, not_2_out);
  or or_3 (or_3_out, A, B, not_1_out, D);
  or or_4 (or_4_out, A, B, not_1_out, not_2_out);
  or or_5 (or_5_out, A, not_4_out, C, not_2_out);
  or or_6 (or_6_out, A, not_4_out, not_1_out, D);
  or or_7 (or_7_out, A, not_4_out, not_1_out, not_2_out);
  or or_8 (or_8_out, not_3_out, B, not_1_out, D);
  or or_9 (or_9_out, not_3_out, B, not_1_out, not_2_out);
  or or_10 (or_10_out, not_3_out, not_4_out, not_1_out, not_2_out);
  or or_11 (or_11_out, A, B, C, D);
  or or_12 (or_12_out, A, not_4_out, C, D);
  or or_13 (or_13_out, A, not_4_out, C, not_2_out);
  or or_14 (or_14_out, not_3_out, B, C, D);
  or or_15 (or_15_out, not_3_out, B, C, not_2_out);
  or or_16 (or_16_out, not_3_out, B, not_1_out, D);
  or or_17 (or_17_out, not_3_out, not_4_out, C, D);
  or or_18 (or_18_out, not_3_out, not_4_out, C, not_2_out);
  or or_19 (or_19_out, not_3_out, not_4_out, not_1_out, D);
  or or_20 (or_20_out, not_3_out, not_4_out, not_1_out, not_2_out);
  or or_21 (or_21_out, A, B, C, not_2_out);
  or or_22 (or_22_out, A, B, not_1_out, D);
  or or_23 (or_23_out, A, B, not_1_out, not_2_out);
  or or_24 (or_24_out, A, not_4_out, C, D);
  or or_25 (or_25_out, A, not_4_out, not_1_out, D);
  or or_26 (or_26_out, A, not_4_out, not_1_out, not_2_out);
  or or_27 (or_27_out, not_3_out, B, C, D);
  or or_28 (or_28_out, not_3_out, B, C, not_2_out);
  or or_29 (or_29_out, not_3_out, B, not_1_out, not_2_out);
  or or_30 (or_30_out, not_3_out, not_4_out, C, D);
  or or_31 (or_31_out, not_3_out, not_4_out, C, not_2_out);
  or or_32 (or_32_out, not_3_out, not_4_out, not_1_out, D);
  and and_1 (Z1, or_1_out, or_2_out, or_3_out, or_4_out, or_5_out, or_6_out, or_7_out, or_8_out, or_9_out, or_10_out);
  and and_2 (Z2, or_11_out, or_12_out, or_13_out, or_14_out, or_15_out, or_16_out, or_17_out, or_18_out, or_19_out, or_20_out);
  and and_3 (Z3, or_21_out, or_22_out, or_23_out, or_24_out, or_25_out, or_26_out, or_27_out, or_28_out, or_29_out, or_30_out, or_31_out, or_32_out);
endmodule
