// Digital circuit Template.dig as structural Verilog
module Template (
  input  X0,
  input  X1,
  input  Selector,
  output Z
);

  wire not_1_out, not_2_out, not_3_out, or_1_out, or_2_out, or_3_out, or_4_out;

  not not_1 (not_1_out, X1);
  not not_2 (not_2_out, Selector);
  not not_3 (not_3_out, X0);
  or or_1 (or_1_out, Selector, X1, X0);
  or or_2 (or_2_out, Selector, not_1_out, X0);
  or or_3 (or_3_out, not_2_out, X1, X0);
  or or_4 (or_4_out, not_2_out, X1, not_3_out);
  and and_1 (Z, or_1_out, or_2_out, or_3_out, or_4_out);
endmodule
